# Fritzing sketch ADXL345StepperUno9V (saved by Fritzing 0.9.2b)

parts:
  Part1 = Arduino Uno (Rev3) - ICSP
  part = Battery block 9V
  M2 = Stepper Motor - Bipolar
  Part2 = EasyDriver_v44
  Part3 = Triple Axis Accelerometer Breakout - ADXL345

nets:
  5V: Part1.5V, Part2.VCC
  N1: Part1.D10_PWM/SS, Part3.CS
  N2: Part1.D11_PWM/MOSI, Part3.SDA
  N3: Part1.D12/MISO, Part3.SDO
  N4: Part1.D13/SCK, Part3.SCL
  GND: Part1.GND, part.-, Part2.GND, Part3.GND
  N5: Part1.D2, Part2.STEP
  N6: Part1.D3_PWM, Part2.DIR
  N7: Part1.D4, Part2.MS1
  N8: Part1.D5_PWM, Part2.MS2
  N9: Part1.D6_PWM, Part2.ENABLE
  3V3: Part1.3V3, Part3.VCC
  N10: Part1.VIN, part.+, Part2.V+
  N11: M2.A, Part2.OUT2A
  N12: M2.C, Part2.OUT2B
  N13: M2.B, Part2.OUT1A
  N14: M2.D, Part2.OUT1B
